// Logisim project fpga.circ as structural Verilog: 15 circuits, main circuit main
module main (
  input  [3:0] in_1,
  input  A,
  input  B,
  output out_4
);

  wire and2_1_out_3, and2_2_out_3, and2_3_out_3, and2_4_out_3, button_1_out, not_1_out, not_2_out;
  wire [3:0] register_1_q;

  Button button_1 (.out(button_1_out));
  not not_1 (not_1_out, A);
  not not_2 (not_2_out, B);
  and2 and2_1 (.in_1(not_1_out), .in_2(not_2_out), .out_3(and2_1_out_3));
  and2 and2_2 (.in_1(not_1_out), .in_2(B), .out_3(and2_2_out_3));
  and2 and2_3 (.in_1(A), .in_2(not_2_out), .out_3(and2_3_out_3));
  and2 and2_4 (.in_1(A), .in_2(B), .out_3(and2_4_out_3));
  Register #(.width(4)) register_1 (.D(in_1), .clk(button_1_out), .Q(register_1_q));  // open: en, clr
  sigif sigif_1 (.sig(register_1_q[3]), .cond(and2_1_out_3), .out_3(out_4));
  sigif sigif_2 (.sig(register_1_q[2]), .cond(and2_2_out_3), .out_3(out_4));
  sigif sigif_3 (.sig(register_1_q[1]), .cond(and2_3_out_3), .out_3(out_4));
  sigif sigif_4 (.sig(register_1_q[0]), .cond(and2_4_out_3), .out_3(out_4));

  // Notes on the sheet:
  //   A0 B0
  //   A0 B1
  //   A1 B0
  //   A1 B1
endmodule

module dissipation_zone (
  input  in_1,
  output out_2
);

  wire transistor_1_out, transistor_2_out, transistor_3_out, transistor_4_out;

  Transistor #(.\type ("n"), .gate("br")) transistor_1 (.in(1'b1), .out(transistor_1_out), .gate(in_1));
  Transistor #(.\type ("n"), .gate("br")) transistor_2 (.in(1'b1), .out(transistor_2_out), .gate(in_1));
  Transistor transistor_3 (.in(1'b0), .out(transistor_3_out), .gate(in_1));
  Transistor transistor_4 (.in(1'b0), .out(transistor_4_out), .gate(in_1));
  Transistor #(.\type ("n"), .gate("br")) transistor_5 (.in(transistor_1_out), .out(out_2), .gate(transistor_2_out));
  Transistor transistor_6 (.in(transistor_4_out), .out(out_2), .gate(transistor_3_out));
endmodule

module inv (
  input  in_1,
  output out_2
);

  wire transistor_1_out, transistor_2_out, transistor_3_out, transistor_4_out;

  Transistor #(.gate("br")) transistor_1 (.in(1'b1), .out(transistor_1_out), .gate(in_1));
  Transistor #(.gate("br")) transistor_2 (.in(1'b1), .out(transistor_2_out), .gate(in_1));
  Transistor #(.\type ("n")) transistor_3 (.in(1'b0), .out(transistor_3_out), .gate(in_1));
  Transistor #(.\type ("n")) transistor_4 (.in(1'b0), .out(transistor_4_out), .gate(in_1));
  Transistor #(.\type ("n"), .gate("br")) transistor_5 (.in(transistor_1_out), .out(out_2), .gate(transistor_2_out));
  Transistor transistor_6 (.in(transistor_4_out), .out(out_2), .gate(transistor_3_out));
endmodule

module sig_sel (
  input  in_1,
  input  in_2,
  input  in_3,
  output out_4
);

  wire transistor_1_out, transistor_2_out, transistor_3_out, transistor_4_out;

  Transistor #(.\type ("n"), .gate("br")) transistor_1 (.in(in_1), .out(transistor_1_out), .gate(in_2));
  Transistor #(.\type ("n"), .gate("br")) transistor_2 (.in(in_2), .out(transistor_2_out), .gate(in_2));
  Transistor transistor_3 (.in(in_2), .out(transistor_3_out), .gate(in_2));
  Transistor transistor_4 (.in(in_3), .out(transistor_4_out), .gate(in_2));
  Transistor #(.\type ("n"), .gate("br")) transistor_5 (.in(transistor_1_out), .out(out_4), .gate(transistor_2_out));
  Transistor transistor_6 (.in(transistor_4_out), .out(out_4), .gate(transistor_3_out));
endmodule

module and2 (
  input  in_1,
  input  in_2,
  output out_3
);

  wire transistor_1_out, transistor_2_out, transistor_3_out, transistor_4_out;

  Transistor #(.\type ("n"), .gate("br")) transistor_1 (.in(in_1), .out(transistor_1_out), .gate(in_2));
  Transistor #(.\type ("n"), .gate("br")) transistor_2 (.in(in_2), .out(transistor_2_out), .gate(in_2));
  Transistor transistor_3 (.in(in_2), .out(transistor_3_out), .gate(in_2));
  Transistor transistor_4 (.in(in_2), .out(transistor_4_out), .gate(in_2));
  Transistor #(.\type ("n"), .gate("br")) transistor_5 (.in(transistor_1_out), .out(out_3), .gate(transistor_2_out));
  Transistor transistor_6 (.in(transistor_4_out), .out(out_3), .gate(transistor_3_out));
endmodule

module or2 (
  input  in_1,
  input  in_2,
  output out_3
);

  wire transistor_1_out, transistor_2_out, transistor_3_out, transistor_4_out;

  Transistor #(.\type ("n"), .gate("br")) transistor_1 (.in(in_1), .out(transistor_1_out), .gate(in_1));
  Transistor #(.\type ("n"), .gate("br")) transistor_2 (.in(in_1), .out(transistor_2_out), .gate(in_1));
  Transistor transistor_3 (.in(in_1), .out(transistor_3_out), .gate(in_1));
  Transistor transistor_4 (.in(in_2), .out(transistor_4_out), .gate(in_1));
  Transistor #(.\type ("n"), .gate("br")) transistor_5 (.in(transistor_1_out), .out(out_3), .gate(transistor_2_out));
  Transistor transistor_6 (.in(transistor_4_out), .out(out_3), .gate(transistor_3_out));
endmodule

module xor2 (
  input  a,
  input  b,
  output out_3
);

  wire and2_1_out_3, inv_1_out_2, or2_1_out_3;

  or2 or2_1 (.in_1(a), .in_2(b), .out_3(or2_1_out_3));
  and2 and2_1 (.in_1(a), .in_2(b), .out_3(and2_1_out_3));
  inv inv_1 (.in_1(and2_1_out_3), .out_2(inv_1_out_2));
  and2 and2_2 (.in_1(or2_1_out_3), .in_2(inv_1_out_2), .out_3(out_3));
endmodule

module nand2 (
  input  in_1,
  input  in_2,
  output out_3
);

  wire and2_1_out_3;

  and2 and2_1 (.in_1(in_1), .in_2(in_2), .out_3(and2_1_out_3));
  inv inv_1 (.in_1(and2_1_out_3), .out_2(out_3));
endmodule

module nor2 (
  input  in_1,
  input  in_2,
  output out_3
);

  wire or2_1_out_3;

  inv inv_1 (.in_1(or2_1_out_3), .out_2(out_3));
  or2 or2_1 (.in_1(in_1), .in_2(in_2), .out_3(or2_1_out_3));
endmodule

module nxor2 (
  input  in_1,
  input  in_2,
  output out_3
);

  wire xor2_1_out_3;

  xor2 xor2_1 (.a(in_1), .b(in_2), .out_3(xor2_1_out_3));
  inv inv_1 (.in_1(xor2_1_out_3), .out_2(out_3));
endmodule

module sigif (
  input  sig,
  input  cond,
  output out_3
);

  wire transistor_1_out, transistor_2_out;

  Transistor #(.\type ("n"), .gate("br")) transistor_1 (.in(sig), .out(transistor_1_out), .gate(cond));
  Transistor #(.\type ("n"), .gate("br")) transistor_2 (.in(cond), .out(transistor_2_out), .gate(cond));
  Transistor #(.\type ("n"), .gate("br")) transistor_3 (.in(transistor_1_out), .out(out_3), .gate(transistor_2_out));
endmodule

module boolean_function (
  input  [3:0] f,
  input  f_we,
  input  f_set,
  input  f_reset,
  input  a,
  input  b,
  output out_7
);

  wire and2_1_out_3, and2_2_out_3, and2_3_out_3, and2_4_out_3, inv_1_out_2, not_1_out, not_2_out;
  wire [3:0] register_1_q;

  not not_1 (not_1_out, a);
  not not_2 (not_2_out, b);
  inv inv_1 (.in_1(f_we), .out_2(inv_1_out_2));
  and2 and2_1 (.in_1(not_1_out), .in_2(not_2_out), .out_3(and2_1_out_3));
  and2 and2_2 (.in_1(not_1_out), .in_2(b), .out_3(and2_2_out_3));
  and2 and2_3 (.in_1(a), .in_2(not_2_out), .out_3(and2_3_out_3));
  and2 and2_4 (.in_1(a), .in_2(b), .out_3(and2_4_out_3));
  Register #(.width(4)) register_1 (.D(f), .en(inv_1_out_2), .clk(f_set), .Q(register_1_q), .clr(f_reset));
  sigif sigif_1 (.sig(register_1_q[3]), .cond(and2_1_out_3), .out_3(out_7));
  sigif sigif_2 (.sig(register_1_q[2]), .cond(and2_2_out_3), .out_3(out_7));
  sigif sigif_3 (.sig(register_1_q[1]), .cond(and2_3_out_3), .out_3(out_7));
  sigif sigif_4 (.sig(register_1_q[0]), .cond(and2_4_out_3), .out_3(out_7));

  // Notes on the sheet:
  //   A0 B0
  //   A0 B1
  //   A1 B0
  //   A1 B1
endmodule

module fpga_cell (
  input  [11:0] CELL_CODE,
  input  in_2,
  input  in_3,
  input  in_4,
  input  in_5,
  output out_6,
  output out_7,
  output out_8,
  output out_9,
  output out_10
);

  wire chain_selector2_1_clko, chain_selector2_1_is_it_you, chain_selector2_1_pwro, chain_selector2_1_ro;

  chain_selector2 chain_selector2_1 (
    .PWR(in_3), .CLK(in_3), .R(in_4), .IS_IT_ME(in_5), .PWRO(chain_selector2_1_pwro),
    .CLKO(chain_selector2_1_clko), .RO(chain_selector2_1_ro), .IS_IT_YOU(chain_selector2_1_is_it_you));
  boolean_function boolean_function_1 ();  // open: f, f_we, f_set, f_reset, a, b, out_7
  chain_selector2 chain_selector2_2 (
    .PWR(chain_selector2_1_pwro), .CLK(chain_selector2_1_clko), .R(chain_selector2_1_ro),
    .IS_IT_ME(chain_selector2_1_is_it_you), .PWRO(out_7), .CLKO(out_8), .RO(out_9), .IS_IT_YOU(out_10));
  Register register_1 ();  // open: D, en, Q, clk, clr

  // Notes on the sheet:
  //   use f1 as a
  //   ...
  //   use f_reset as a
  //   use a as f1
  //   ...
  //   use a as f_reset
endmodule

module chain_selector (
  input  CLK,
  input  RST,
  input  IS_IT_ME
);

  wire inv_1_out_2, inv_2_out_2, register_1_q, register_3_q;

  Register #(.width(1)) register_1 (.D(CLK), .clk(CLK), .Q(register_1_q), .clr(RST));  // open: en
  Register register_2 ();  // open: D, en, Q, clk, clr
  Register #(.width(1)) register_3 (.D(register_1_q), .clk(inv_1_out_2), .Q(register_3_q), .clr(RST));  // open: en
  inv inv_1 (.in_1(CLK), .out_2(inv_1_out_2));
  Register #(.width(1)) register_4 (.D(register_3_q), .clk(inv_2_out_2));  // open: en, Q, clr
  inv inv_2 (.in_1(inv_1_out_2), .out_2(inv_2_out_2));
endmodule

module chain_selector2 (
  input  PWR,
  input  CLK,
  input  R,
  input  IS_IT_ME,
  output PWRO,
  output CLKO,
  output RO,
  output IS_IT_YOU
);

  Register #(.width(1)) register_1 (.D(PWR), .clk(CLK), .Q(PWRO), .clr(R));  // open: en
  inv inv_1 (.in_1(CLK), .out_2(CLKO));

  assign IS_IT_YOU = IS_IT_ME;
  assign RO = R;
endmodule
